# Fritzing sketch OIC_Projeto (saved by Fritzing 0.9.3b)
breadboards: 1

parts:
  RHT1 = Humidity and Temperature Sensor RHT03
  SG1 = Buzzer 12mm [package=buzzer-ccv-kit]
  U1 = NodeMCU V3.0
  LED8 = LED - 3mm [color="Green (555nm)" package="3 mm [THT]"]
  LED9 = LED - 3mm [color="Yellow (585nm)" package="3 mm [THT]"]
  LED10 = LED - 3mm [color="Red (635nm)" package="3 mm [THT]"]
  R1 = Resistor [tolerance=±5% resistance=220 package="2512 [SMD]"]
  R2 = Resistor [tolerance=±5% resistance=220 package="1206 [SMD]"]
  R3 = Resistor [tolerance=±5% resistance=220 package="1206 [SMD]"]
  R4 = Resistor [tolerance=±5% resistance=220 package="1206 [SMD]"]
  LED12 = LED - 3mm [color="Blue (430nm)" package="3 mm [THT]"]

nets:
  N1: RHT1.Data-signal, U1.A0
  N2: RHT1.GND_1, U1.GND#41, LED8.cathode, LED9.cathode, LED10.cathode, LED12.cathode
  N3: RHT1.GND_2, U1.D0
  N4: SG1.1, U1.D5
  N5: SG1.2, U1.GND#6, U1.GND#16
  N6: U1.D1, R1.Pin_1
  N7: U1.D2, R2.Pin_1
  N8: U1.D3, R3.Pin_1
  N9: U1.D4, R4.Pin_1

custom parts:
  NodeMCU V3.0: ESP8266 based NodeMCU
